# Fritzing sketch iotlab1 (saved by Fritzing 0.9.3b)
breadboards: 1

parts:
  Raspberry_Pi_1 = Raspberry Pi 3 [part_number=RPI-3-V1.2]  # not connected
  Part1 = Arduino Uno (Rev3)
  Part2 = Arduino Uno (Rev3)  # not connected
  Part3 = Arduino Ethernet Shield (Rev3)
  M1 = Niren can bus module [package=THT]
  M2 = Niren can bus module [package=THT]
  HC-SR04_Sensor_1 = HC-SR04 Ultrasonic Distance Sensor
  LED1 = smd LED [color="Red (633nm)" package="0805 [SMD]"]
  R1 = Resistor [tolerance=±5% resistance=220 package=THT]
  R2 = Resistor [tolerance=±5% resistance=220 package="2010 [SMD]"]
  R3 = Resistor [tolerance=±5% resistance=220 package="2010 [SMD]"]

nets:
  N1: Part1.D8, LED1.anode
  N2: Part1.D10_PWM/SS, M2.pin3
  N3: Part1.D11_PWM/MOSI, M2.pin5
  N4: Part1.D12/MISO, M2.pin4
  N5: Part1.D13/SCK, M2.pin6
  GND: Part1.GND, M2.pin2, HC-SR04_Sensor_1.GND, R1.Pin_0
  N6: Part1.D2, M2.pin7
  N7: Part1.D6_PWM, HC-SR04_Sensor_1.ECHO
  N8: Part1.D7, HC-SR04_Sensor_1.TRIG
  5V: Part1.5V, M2.pin1, HC-SR04_Sensor_1.VCC
  N9: Part3.ETH_CS, M1.pin3
  N10: Part3.PWM_D11, M1.pin5
  N11: Part3.SPI/D12, M1.pin4
  N12: Part3.SPI/D13, M1.pin6
  N13: Part3.D2, M1.pin7
  N14: Part3.5V, M1.pin1
  N15: Part3.GND, M1.pin2
  N16: M1.pin10, M1.pin12, M2.pin10, M2.pin12, R2.Pin_1, R3.Pin_1
  N17: M1.pin11, M1.pin13, M2.pin11, M2.pin13, R2.Pin_0, R3.Pin_0
  N18: LED1.cathode, R1.Pin_1

notes:
  Ethernet Shield On top of Arduino Uno

custom parts:
  Niren can bus module: Niren can bus module availabe on ebay and others. No pcb view as no mechanical drawng and it wouldn't mount anyway.
